# Fritzing sketch LED_Flame (saved by Fritzing 0.9.4)
breadboards: 1

parts:
  R1 = Resistor [tolerance=±5% resistance=220 package=THT]
  R2 = Resistor [tolerance=±5% resistance=220 package=THT]
  LED1 = LED - 5mm [color="Yellow (595nm)" package="5 mm [THT]"]
  LED2 = LED - 5mm [color="Yellow (595nm)" package="5 mm [THT]"]
  R3 = Resistor [tolerance=±5% resistance=220 package=THT]
  LED3 = LED - 5mm [color="Yellow (595nm)" package="5 mm [THT]"]
  R4 = Resistor [tolerance=±5% resistance=220 package=THT]
  LED4 = LED - 5mm [color="Yellow (595nm)" package="5 mm [THT]"]
  R5 = Resistor [tolerance=±5% resistance=220 package=THT]
  LED5 = LED - 5mm [color="Yellow (595nm)" package="5 mm [THT]"]
  U1 = Arduino Uno (Rev3)

nets:
  N1: R1.Pin_0, LED1.anode
  N2: R1.Pin_1, U1.D11_PWM/MOSI
  N3: R2.Pin_0, LED2.anode
  N4: R2.Pin_1, U1.D10_PWM/SS
  N5: LED1.cathode, LED2.cathode, LED3.cathode, LED4.cathode, LED5.cathode, U1.GND
  N6: R3.Pin_0, LED3.anode
  N7: R3.Pin_1, U1.D9_PWM
  N8: R4.Pin_0, LED4.anode
  N9: R4.Pin_1, U1.D6_PWM
  N10: R5.Pin_0, LED5.anode
  N11: R5.Pin_1, U1.D5_PWM
